# Fritzing sketch schema (saved by Fritzing 0.9.3b)
circuit board: 8.46667cm x 5.64444cm
breadboards: 1

parts:
  Power_plug1 = Power plug
  Q2 = TRANSISTOR_NPN [package=to-92-ammo]
  Q3 = TRANSISTOR_NPN [package=to-92-ammo]
  Q4 = TRANSISTOR_NPN [package=to-92-ammo]
  Q5 = TRANSISTOR_NPN [package=to-92-ammo]
  LED2 = smd LED [color="Red (633nm)" package="0603 [SMD]"]
  LED3 = smd LED [color="Yellow (592nm)" package="0603 [SMD]"]
  LED5 = smd LED [color="Blue (430nm)" package="0603 [SMD]"]
  LED6 = smd LED [color="Green (555nm)" package="0603 [SMD]"]
  D1 = Rectifier Diode [part_number=1N4001 package="Melf DO-213 AB [SMD]"]
  R3 = Resistor [tolerance=±5% resistance=220 package=THT]
  R4 = Resistor [tolerance=±5% resistance=220 package=THT]
  R5 = Resistor [tolerance=±5% resistance=220 package=THT]
  R6 = Resistor [tolerance=±5% resistance=220 package=THT]
  S8 = Pushbutton [package=THT]
  S9 = Pushbutton [package=THT]
  S10 = Pushbutton [package=THT]
  S11 = Pushbutton [package=THT]
  X1 = USB Connectors [package=usb-a-s-nosilk-female]
  X2 = USB Connectors [package=usb-a-s-nosilk-female]
  X3 = USB Connectors [package=usb-a-s-nosilk-female]
  X4 = USB Connectors [package=usb-a-s-nosilk-female]
  Raspberry_Pi_1 = Raspberry Pi 3 [part_number=RPI-3-V1.2]

nets:
  GND: Power_plug1.GND, LED2.cathode, LED3.cathode, LED5.cathode, LED6.cathode, X1.GND, X2.GND, X3.GND, X4.GND
  N1: Power_plug1.VCC, Q2.C, Q3.C, Q4.C, Q5.C, D1.anode, S8.leg1, S9.leg1, S10.leg1, S11.leg1, X1.D-, X2.D-, X3.D-, X4.D-
  N2: Q2.E, Raspberry_Pi_1.GPIO26
  N3: Q2.B, LED2.anode, X4.VBUS
  N4: Q3.E, Raspberry_Pi_1.GPIO13
  N5: Q3.B, LED3.anode, X3.VBUS
  N6: Q4.E, Raspberry_Pi_1.GPIO9
  N7: Q4.B, LED5.anode, X2.VBUS
  N8: Q5.E, Raspberry_Pi_1.GPIO22
  N9: Q5.B, LED6.anode, X1.VBUS
  N10: D1.cathode, Raspberry_Pi_1.GND
  N11: R3.Pin_0, S9.leg0, X2.D+, Raspberry_Pi_1.GPIO10
  N12: R3.Pin_1, R4.Pin_1, R5.Pin_1, R6.Pin_1, Raspberry_Pi_1.3v3
  N13: R4.Pin_0, S8.leg0, X1.D+, Raspberry_Pi_1.GPIO27
  N14: R5.Pin_0, S10.leg0, X3.D+, Raspberry_Pi_1.GPIO11
  N15: R6.Pin_0, S11.leg0, X4.D+, Raspberry_Pi_1.GPIO19
